# Fritzing sketch profMeasurement (saved by Fritzing 0.9.4)
breadboards: 1

parts:
  IC1 = AD620 [package=dip08]
  R1 = Resistor [tolerance=±5% resistance=5.6k package=THT]
  Part1 = Arduino Uno (Rev3)
  R2 = Resistor [tolerance=±5% resistance=180k package=THT]
  C1 = Ceramic Capacitor [capacitance=100nF package="100 mil [THT, multilayer]"]
  C2 = Ceramic Capacitor [capacitance=22nF package="100 mil [THT, multilayer]"]
  VCC2 = Battery block 9V
  R5 = Resistor [tolerance=±5% resistance=180k package=THT]
  R4 = Resistor [tolerance=±5% resistance=100k package=THT]
  VCC1 = Battery block 9V
  IC2 = IC, DIP package, 8 pins [chip_label=IC]  # not connected

nets:
  N1: IC1.R_G#0, R1.Pin_0
  N2: IC1.V-, VCC2.-
  GND: IC1.REF, C1.0
  N3: IC1.OUT, R2.Pin_0
  N4: IC1.V+, VCC1.+
  N5: IC1.R_G#7, R1.Pin_1
  N6: Part1.A0, C2.0, R4.Pin_1
  N7: R2.Pin_1, C1.1, R5.Pin_1, R4.Pin_0
  N8: C2.1, R5.Pin_0
  N9: VCC2.+, VCC1.-

custom parts:
  AD620: Instrument Amp
