# Fritzing sketch wheatstone (saved by Fritzing 0.9.4)
breadboards: 1

parts:
  LM358 = LM 358 Dual Op-Amp [package="DIP8 [THT]"]
  R1 = Resistor [tolerance=±5% resistance=4.7k package=THT]
  C1 = Electrolytic Capacitor [capacitance=1µF package="100 mil [THT, electrolytic]"]
  R2 = Resistor [tolerance=±5% resistance=1k package=THT]
  R3 = Resistor [tolerance=±5% resistance=1k package=THT]
  R4 = Resistor upright [tolerance=±5% resistance=3.3M package=THT]
  R5 = Resistor [tolerance=±5% resistance=4.7M package=THT]
  R6 = Resistor [tolerance=±5% resistance=3.3M package=THT]
  Part1 = Arduino Uno (Rev3)
  Plant = Resistor [tolerance=±5% resistance=220 package=THT]
  R8 = Trimmer Potentiometer [maximum_resistance=100kΩ package=THT]
  R7 = Resistor [tolerance=±5% resistance=1M package=THT]

nets (from the breadboard view):
  N1: LM358.connector0, R1.Pin_0, R4.Pin_1
  N2: LM358.connector1, R2.Pin_1, R4.Pin_0
  N3: LM358.connector2, R3.Pin_1
  N4: LM358.connector3, C1.-, Plant.Pin_0, R7.Pin_0
  N5: LM358.connector7, R5.Pin_0, R6.Pin_1
  N6: R1.Pin_1, C1.+, Part1.A1
  N7: R2.Pin_0, R8.wiper
  N8: R3.Pin_0, R6.Pin_0, Plant.Pin_1
  N9: R5.Pin_1, R8.leg1
  N10: R8.leg2, R7.Pin_1

custom parts:
  Resistor upright: A generic upright standing resistor (0.25W)
